# Fritzing sketch BZen-BC1-1.0.0-dev (saved by Fritzing 0.9.2b)
breadboards: 1

parts:
  U1 = Voltage Regulator - 5V [part_number=UA78M05 package="TO220 [THT]"]
  C1 = Ceramic Capacitor [capacitance=100nF voltage=20V part_number=RDER71E104K0K1H03B package="100 mil [THT, multilayer]"]
  C2 = Ceramic Capacitor [capacitance=1µF part_number=FG18X7R1E105KRT06 voltage=20V package="100 mil [THT, multilayer]"]
  C3 = Ceramic Capacitor [capacitance=100nF voltage=20V part_number=FA14X8R1E334KNU06 package="100 mil [THT, multilayer]"]
  C4 = Ceramic Capacitor [capacitance=100nF voltage=20V part_number=RDER71E104K0K1H03B package="100 mil [THT, multilayer]"]
  C5 = Ceramic Capacitor [capacitance=100nF voltage=20V part_number=RDER71E104K0K1H03B package="100 mil [THT, multilayer]"]
  C6 = Ceramic Capacitor [capacitance=100nF voltage=20V part_number=RDER71E104K0K1H03B package="100 mil [THT, multilayer]"]
  R1 = Resistor [tolerance=±5% resistance=1k package=THT]
  R2 = Resistor [tolerance=±5% resistance=4.7k package=THT]
  R3 = Resistor [tolerance=±5% resistance=10k package=THT]
  R4 = Resistor [tolerance=±5% resistance=10k package=THT]
  R5 = Resistor [tolerance=±5% resistance=10k package=THT]
  R6 = Resistor [tolerance=±5% resistance=10k package=THT]
  Q1 = PNP-Transistor [part_number=2N3906 package="TO92 [THT]"]
  Q2 = NPN-Transistor [part_number=2N3904 package="TO92 [THT]"]
  Q3 = NPN-Transistor [part_number=ZTX451 package="TO92 [THT]"]
  Q4 = NPN-Transistor [part_number=2N3904 package="TO92 [THT]"]
  Q5 = PNP-Transistor [part_number=ZTX789 package="TO92 [THT]"]
  D1 = Rectifier Diode [part_number=1N4148 package="300 mil [THT]"]
  C7 = Ceramic Capacitor [capacitance=10nF voltage=20V part_number=SR215C103KAATR1 package="100 mil [THT, multilayer]"]
  C9 = Ceramic Capacitor [capacitance=470pF voltage=20V package="100 mil [THT, multilayer]"]
  C10 = Electrolytic Capacitor [capacitance=47µF voltage=20V part_number=ULD1E470MDD1TD package="100 mil [THT, electrolytic]"]
  D2 = Rectifier Diode [part_number=SB130 package="300 mil [THT]"]
  L1 = Inductor [inductance=10µH part_number=77F100K-TR-RC package="400 mil [THT]"]
  LED1 = LED - 5mm [color="Red (633nm)" package="5 mm [THT]"]
  LED2 = LED - 5mm [color="Green (555nm)" package="5 mm [THT]"]
  R7 = Resistor [tolerance=±5% resistance=1k package=THT]
  R8 = Resistor [tolerance=±5% resistance=0 package=THT]
  R9 = Resistor [tolerance=±5% resistance=220 package=THT]
  R10 = Resistor [tolerance=±5% resistance=62k package=THT]
  R11 = Resistor [tolerance=±5% resistance=10k package=THT]
  R12 = Resistor [tolerance=±5% resistance=10k package=THT]
  R13 = Resistor [tolerance=±5% resistance=1k package=THT]
  D3 = Rectifier Diode [part_number=SB130 package="300 mil [THT]"]
  L2 = Inductor [package="400 mil [THT]"]
  R14 = Resistor [tolerance=±1% resistance=100k package=THT]
  R15 = Resistor [tolerance=±5% resistance=93.50k package=THT]
  C11 = Tantalum Capacitor [capacitance=1μF package="100 mil [THT, tantalum]"]
  IC1 = IC, DIP package, 16 pins [chip_label=IC1]
  C8 = Ceramic Capacitor [capacitance=1nF voltage=20V package="100 mil [THT, multilayer]"]

nets:
  N1: U1.input_voltage, C3.0, D2.anode
  N2: U1.GND, C1.0, C2.0, C3.1, C6.0, R6.Pin_1, Q4.E, C7.0, C9.1, C10.-, R8.Pin_0, R9.Pin_1, R12.Pin_1, D3.anode, IC1.pin12
  N3: U1.output_voltage, C2.1, C4.0, C4.1, C5.0, C6.1, R10.Pin_0, IC1.pin6, IC1.pin13
  N4: C1.1, IC1.pin5
  N5: C5.1, IC1.pin4
  N6: R1.Pin_0, Q2.E, Q5.B, D1.anode, L1.pin_1
  N7: R1.Pin_1, Q2.C, Q5.E
  N8: R2.Pin_0, Q1.C
  N9: R2.Pin_1, L2.pin_1, R14.Pin_1, C11.+
  N10: R3.Pin_0, IC1.pin10
  N11: R3.Pin_1, Q4.B
  N12: R4.Pin_0, R5.Pin_1, Q1.B
  N13: R4.Pin_1, Q1.E, C10.+, D2.cathode
  N14: R5.Pin_0, Q4.C
  N15: R6.Pin_0, LED2.anode, IC1.pin16
  N16: Q2.B, Q3.C, D1.cathode, L1.pin_0
  N17: Q3.E, R9.Pin_0
  N18: Q3.B, IC1.pin14
  N19: Q5.C, D3.cathode, L2.pin_0
  N20: C7.1, R7.Pin_0, IC1.pin7, C8.0
  N21: C9.0, IC1.pin9
  N22: LED1.cathode, LED2.cathode, R13.Pin_0
  N23: LED1.anode, IC1.pin15
  N24: R7.Pin_1, R8.Pin_1, R11.Pin_1, R15.Pin_0, C11.-
  N25: R10.Pin_1, IC1.pin1
  N26: R11.Pin_0, R12.Pin_0, IC1.pin8
  N27: R13.Pin_1, IC1.pin11
  N28: R14.Pin_0, R15.Pin_1, IC1.pin3, C8.1
